# Fritzing sketch mp3playerir (saved by Fritzing 0.9.3b)
circuit board: 14.1864cm x 5.43748cm
breadboards: 1

parts:
  Part1 = Arduino Uno (Rev3) - ICSP
  SP1 = SPEAKER [package=pcb_mount_speaker]
  DFPlayer_Mini1 = DFPlayer MINI [package="DIP (Dual Inline) [THT]"]
  Mod1 = KY-022 Infrared Receiver Module [package="Breakout board"]
  R1 = Resistor [tolerance=±5% resistance=1k package="0805 [SMD]"]

nets:
  N1: Part1.D10_PWM/SS, DFPlayer_Mini1.TX
  N2: Part1.D11_PWM/MOSI, R1.Pin_0
  N3: Part1.D6_PWM, Mod1.S
  5V: Part1.5V, DFPlayer_Mini1.VCC, Mod1.Vin
  N4: Part1.GND, DFPlayer_Mini1.GND#6, Mod1.-
  N5: SP1.+, DFPlayer_Mini1.SPK2
  N6: SP1.-, DFPlayer_Mini1.SPK1
  N7: DFPlayer_Mini1.RX, R1.Pin_1
  N8: DFPlayer_Mini1.IO_1, DFPlayer_Mini1.K1/ADC_KEY, DFPlayer_Mini1.USB_-

custom parts:
  DFPlayer MINI: MP3 module by DFRobot.com for playing Music from an SD-Card. Supports WAV and MP3 files.
  KY-022 Infrared Receiver Module: KY-022 IR receiver module, reacts to 38kHz infrared light.
